# Fritzing sketch Schematitc (saved by Fritzing 0.9.3b)

parts:
  U2 = ESP 32 DEVKIT DOIT
  U3 = Nokia 6100 Color LCD [package=nokia6100_lcd]
  Part1 = Solid State High Level Relay Module [package=relay]

nets:
  N1: U2.D19, Part1.CH1
  N2: U2.TX2, U2.RX2, U2.D15, U2.SD1, U3.GND, U3.LEDGND
  N3: U2.VIN, U3.VDISPLAY

notes:
  NX4832T035_011R
  NEXTION 3,5"
  Nexiton Pin Description
  Yellow=TX
  Green=RX

custom parts:
  Solid State High Level Relay Module: 5V Omron solid state relay 240V 2A output with resistance fuse.
